# Fritzing sketch light_sensor_led_sketch (saved by Fritzing 0.9.3b)
breadboards: 1

parts:
  Part1 = Photon
  R1 = PHOTOCELL [package=photocell]
  R2 = Resistor [tolerance=±5% resistance=10k package="0603 [SMD]"]
  LED1 = smd LED [color="Red (633nm)" package="0603 [SMD]"]
  R3 = Resistor [tolerance=±5% resistance=220 package="0603 [SMD]"]

nets:
  N1: Part1.A0, R1.P$2, R2.Pin_0
  N2: Part1.GND, R2.Pin_1, LED1.cathode
  N3: Part1.D0, R3.Pin_1
  N4: Part1.3V3, R1.P$1
  N5: LED1.anode, R3.Pin_0
